# Fritzing sketch 2-Motor_Control_Speed_Two_Motors-L298n_fritzing schematic (saved by Fritzing 0.9.3b)

parts:
  L298N1 = L298N DC motor driver
  Part1 = Arduino Uno (Rev3)
  VCC1 = Battery block 9V
  M3 = DC Motor  # not connected
  M4 = DC Motor  # not connected

nets:
  GND: L298N1.GND, Part1.GND, VCC1.-
  5V: L298N1.5V, Part1.5V
  N1: L298N1.ENA, Part1.D5_PWM
  N2: L298N1.ENB, Part1.D10_PWM/SS
  N3: L298N1.IN1, Part1.D6_PWM
  N4: L298N1.IN2, Part1.D7
  N5: L298N1.IN3, Part1.D8
  N6: L298N1.IN4, Part1.D9_PWM

custom parts:
  L298N DC motor driver: 2x DC motor driver with 78M05 positive voltage regulator (7..35 V) L298N: max 46 V, 2 A Set 5 V Enable jumper to enable 5 V regultor (needed for the L298N) and +5 V output at screw terminal or supply external +5 V at screw terminal Set ENA and/or ENB to +5 V to enable motor permanently or supply ENA and/or ENB with PWM signal IN1 and IN2 set rotation directory for motor A (OUT1/OUT2) IN2 and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
