# Fritzing sketch 4-schematic (saved by Fritzing 0.9.3b)
breadboards: 1

parts:
  Part1 = Arduino Uno (Rev3)
  LED3 = LED - 5mm [color="Red (633nm)" package="5 mm [THT]"]
  LED4 = LED - 5mm [color="Red (633nm)" package="5 mm [THT]"]

nets:
  N1: Part1.D9_PWM, LED3.anode, LED4.anode
  N2: Part1.GND, LED3.cathode, LED4.cathode

notes:
  Two LED in parallel
