# Fritzing sketch 5-power circuit schematic (saved by Fritzing 0.9.3b)
breadboards: 1

parts:
  Power_plug1 = Power plug
  IC1 = Voltage Regulator [package=78xxl]
  Part1 = Arduino Uno (Rev3)
  C1 = Capacitor Polarized [package=panasonic_c]
  C2 = Capacitor Polarized [package=cpol-radial-10uf-25v]  # not connected
  VCC1 = Battery block 9V
  S1 = Round Pushbutton
  LED1 = LED - 5mm [color="Red (633nm)" package="5 mm [THT]"]
  LED2 = LED - 5mm [color="Red (633nm)" package="5 mm [THT]"]
  R1 = Resistor [tolerance=±5% resistance=220 package=THT]
  R2 = Resistor [tolerance=±5% resistance=220 package=THT]

nets:
  GND: Power_plug1.GND, IC1.GND, Part1.GND, C1.-, VCC1.-, LED1.cathode, LED2.cathode
  N1: IC1.IN, C1.+, S1.leg1
  N2: IC1.OUT, Part1.5V
  N3: VCC1.+, S1.leg0, R1.Pin_1, R2.Pin_1
  N4: LED1.anode, R2.Pin_0
  N5: LED2.anode, R1.Pin_0

notes:
  L7805
  DC 9 volt input from adapter
  smothing capacitor
  5volt output to arduino projects
  green=full
  red=Empty
  withen charging open the circuit
